# Fritzing sketch HSU (saved by Fritzing 0.7.10b)
breadboards: 1

parts:
  Nano = Arduino Nano v3.0
  JY-MCU = Generic female header - 4 pins [package=THT]
  R2 = 10k Ω Resistor [package=THT]
  9V_VCC = Battery block 9V
  S1 = Pushbutton [package="[THT]"]
  R3 = 10k Ω Resistor [package=THT]
  LED2 = RGB LED (com. cathode, rgb) [package="5 mm [THT]"]
  R1 = 10k Ω Resistor [package=THT]
  R4 = 150 Ω Resistor [package=THT]
  R5 = 100 Ω Resistor [package=THT]
  R6 = 100 Ω Resistor [package=THT]
  J1 = Generic female header - 7 pins [package=THT]  # not connected

nets:
  N1: Nano.GND, JY-MCU.pin3, 9V_VCC.-, R3.Pin_1, LED2.common_cathode
  N2: Nano.D2, R2.Pin_0
  N3: Nano.D3, R1.Pin_0
  N4: Nano.D4, S1.Pin_3, S1.Pin_4, R3.Pin_0
  N5: Nano.D5, JY-MCU.pin4
  N6: Nano.D6, R4.Pin_0
  N7: Nano.D7, R5.Pin_0
  N8: Nano.D8, R6.Pin_0
  N9: Nano.+5V, S1.Pin_1, S1.Pin_2
  N10: Nano.VIN, 9V_VCC.+
  N11: JY-MCU.pin1, R1.Pin_1
  N12: JY-MCU.pin2, R2.Pin_1
  N13: LED2.red_anode, R4.Pin_1
  N14: LED2.green_anode, R5.Pin_1
  N15: LED2.blue_anode, R6.Pin_1

notes:
  HSU Main Board v1.0
  JY-MCU Width = 16.04 mm
  JY-MCU Height = 36.12 mm
